# Fritzing sketch antipato (saved by Fritzing 0.9.3b)
circuit board: 8.46667cm x 5.64444cm
breadboards: 1

parts:
  Onderdeel1 = Arduino Uno (Rev3)
  LCM1602_IIC1 = LCM1602 IIC [part_number="LCM1602 IIC" chip_label="LCM1602 IIC" package="DIP (Dual Inline) [THT]"]
  LCD1 = LCD screen
  Componente3 = Arduino USB Host Shield  # not connected
  U1 = 4RelayModule
  S1 = Pushbutton [package="[THT]"]
  S2 = Pushbutton [package="[THT]"]
  S3 = Pushbutton [package="[THT]"]
  R1 = Resistor [tolerance=±5% resistance=220 package="2010 [SMD]"]
  R2 = Resistor [tolerance=±5% resistance=220 package="2010 [SMD]"]
  R3 = Resistor [tolerance=±5% resistance=220 package="2010 [SMD]"]
  CONN2 = USB connector [package=THT]
  TO_USB_HOST_SHIELD = USB TTL Serial Cable
  TO_PC = USB TTL Serial Cable
  RUBBER_BEE = FTDI Basic Programmer  # not connected
  part = Adafruit Atmega32u4 Breakout Board  # not connected
  USB_DEVICE = USB TTL Serial Cable  # not connected
  ATTINY85 = Adafruit Trinket 5V  # not connected
  VCC2 = Battery block 9V  # not connected

nets:
  N1: Onderdeel1.A0, U1.IN4
  N2: Onderdeel1.A1, U1.IN3
  N3: Onderdeel1.A2, U1.IN2
  N4: Onderdeel1.A3, U1.IN1
  N5: Onderdeel1.A4/SDA, LCM1602_IIC1.SDA
  N6: Onderdeel1.A5/SCL, LCM1602_IIC1.SCL
  N7: Onderdeel1.D5_PWM, S3.Pin_3, S3.Pin_4, R3.Pin_1
  N8: Onderdeel1.D6_PWM, S2.Pin_3, S2.Pin_4, R2.Pin_1
  N9: Onderdeel1.D7, S1.Pin_3, S1.Pin_4, R1.Pin_1
  VCC: Onderdeel1.5V, LCM1602_IIC1.VCC, U1.VCC, S1.Pin_1, S1.Pin_2, S2.Pin_1, S2.Pin_2, S3.Pin_1, S3.Pin_2
  GND: Onderdeel1.GND, LCM1602_IIC1.GND, U1.GND, R1.Pin_0, R2.Pin_0, R3.Pin_0
  VSS: LCM1602_IIC1.VSS, LCD1.VSS
  VDD: LCM1602_IIC1.VDD, LCD1.VDD
  N10: LCM1602_IIC1.V0, LCD1.V0
  N11: LCM1602_IIC1.RS, LCD1.RS
  N12: LCM1602_IIC1.RW, LCD1.R/W
  N13: LCM1602_IIC1.E, LCD1.E
  N14: LCM1602_IIC1.D0, LCD1.DB0
  N15: LCM1602_IIC1.D1, LCD1.DB1
  N16: LCM1602_IIC1.D2, LCD1.DB2
  N17: LCM1602_IIC1.D3, LCD1.DB3
  N18: LCM1602_IIC1.D4, LCD1.DB4
  N19: LCM1602_IIC1.D5, LCD1.DB5
  N20: LCM1602_IIC1.D6, LCD1.DB6
  N21: LCM1602_IIC1.D7, LCD1.DB7
  N22: LCM1602_IIC1.A, LCD1.LED+
  N23: LCM1602_IIC1.K, LCD1.LED-
  N24: LCM1602_IIC1.LED_A, LCM1602_IIC1.LED_B
  N25: U1.NC1, CONN2.5V
  N26: U1.NO1, TO_PC.5V
  N27: U1.CC1, TO_USB_HOST_SHIELD.5V
  N28: U1.NC2, CONN2.GND, CONN2.chassis5, CONN2.chassis6
  N29: U1.NO2, TO_PC.GND
  N30: U1.CC2, TO_USB_HOST_SHIELD.GND
  N31: U1.NC3, CONN2.d-
  N32: U1.NO3, TO_PC.RX
  N33: U1.CC3, TO_USB_HOST_SHIELD.RX
  N34: U1.NC4, CONN2.d+
  N35: U1.NO4, TO_PC.TX
  N36: U1.CC4, TO_USB_HOST_SHIELD.TX

notes:
  BADUSB, Keyboard USB, Mouse USB, Hard Disk USB, Pendrive, ...

custom parts:
  LCM1602 IIC: I2C-Module to use a 1602 or 2004 LCD on with the wire.h libory Serial LCD Modul
  4RelayModule: 4 relay arduino module SONGLE SRD05VDC-SL-C
  Adafruit Trinket 5V: Trinket may be small, but do not be fooled by its size! It's a tiny microcontroller board, built around the Atmel ATtiny85, a little chip with a lot of power. We wanted to design a microcontroller board that was small enough to fit into any project, and low cost enough to use without hesitation. Perfect for when you don't want to give up your expensive dev-board and you aren't willing to take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

// code stored in the sketch: AnalogReadSerial2LCD_LED.ino
#include <Wire.h>
#include <LiquidCrystal_I2C.h>

LiquidCrystal_I2C lcd(0x27, 16, 2);   // adress and format LCD

const int analogInPin = A0;           // Analog input pin that the potentiometer is attached to
const int analogOutPin = 9;           // Analog output pin that the LED is attached to

int sensorValue = 0;                  // value read from the pot
int outputValue = 0;                  // value output to the PWM (analog out)

void setup() {
  lcd.init();                         // init LCD
  lcd.backlight();
  lcd.home();
  lcd.setCursor(5, 0);                // place static text
  lcd.print("ADC = ");
  lcd.setCursor(15, 0);
  lcd.print("V");
  lcd.setCursor(0, 1);
  lcd.print("LED : ");
  lcd.setCursor(12, 1);
  lcd.print("%");
  Serial.begin(9600);                 // optional serial monitor
}

void loop() {
  int sensorValue = analogRead(analogInPin);          // read analog A0 en store in sensorValue
  float voltValue = 5.0 / 1024.0 * sensorValue;       // calculate volt at analog A0 and store in voltValue
  float percentValue = sensorValue / 1024.0 * 100.0;  // calculate percentage analog A0 and store in percentValue
  outputValue = map(sensorValue, 0, 1023, 0, 255);    // map analog input to analog output and store in outputValue
  analogWrite(analogOutPin, outputValue);             // write outputValue to analogOutPin

  lcd.setCursor(0, 0);                                // set cursor at deserid position
  leadingZeros(sensorValue, 4);                       // print sensorvalue with number of leading-characters (0 or space as specified in function leadingZeros)
  lcd.setCursor(10, 0);                               // set cursor at deserid position
  lcd.print(voltValue);                               // print voltValue
  lcd.setCursor(6, 1);                                // set cursor at deserid position
  lcd.print(percentValue);                            // print percentValue

  Serial.print("sensor = " );                         // print the results to the serial monitor:
  Serial.print(sensorValue);
  Serial.print("\t output = ");
  Serial.print(outputValue);
  Serial.print("\t procent = ");
  Serial.println(percentValue);

  delay(1000);                                        // set delay
}

void leadingZeros( int value, int width) {            // display result with leading characters
  char valueStr[6];                                   // large enough to hold an int
  itoa (value, valueStr, 10);                         // itoa converts int to string
  int len = strlen(valueStr);                         // calculate length of valueStr
  if (len < width) {
    len = width - len;
    while (len--)
      lcd.print(' ');                                 // for leading zeros place '0' between (), for leading spaces place ' ' between ()
  }
  lcd.print(valueStr);
}
